# Fritzing sketch lampenfuss (saved by Fritzing 0.8.3b)
stripboards: 1

parts:
  Bauteil1 = Arduino Pro Mini v13
  Raspberry_Pi_rev1 = Raspberry Pi rev2  # not connected
  M1 = DC Motor

nets:
  N1: Bauteil1.GND, M1.pin_1
